// Logisim project Projeto_ULA.circ as structural Verilog
module ADD_1 (
  input  A,
  input  B,
  input  VAI_1,
  output S,
  output VEM_1
);

  wire and_1_out, and_2_out, not_1_out, or_1_out, xor_1_out;

  xor xor_1 (xor_1_out, A, B);
  not not_1 (not_1_out, A);
  or or_1 (or_1_out, B, VAI_1);
  and and_1 (and_1_out, B, VAI_1);
  xor xor_2 (S, xor_1_out, VAI_1);
  and and_2 (and_2_out, not_1_out, or_1_out);
  main main_1 ();
  or or_2 (VEM_1, and_2_out, and_1_out);
endmodule

module SUB_4 (
  input  [3:0] B,
  input  [3:0] in_2,
  input  VEM_1,
  output overflow,
  output [3:0] saida
);

  wire add_1_2_vem_1, add_1_3_vem_1, add_1_4_vem_1;

  ADD_1 add_1_1 (.A(in_2[3]), .B(B[3]), .VAI_1(add_1_2_vem_1), .S(saida[3]), .VEM_1(overflow));
  main main_1 ();
  ADD_1 add_1_2 (.A(in_2[2]), .B(B[2]), .VAI_1(add_1_3_vem_1), .S(saida[2]), .VEM_1(add_1_2_vem_1));
  main main_2 ();
  ADD_1 add_1_3 (.A(in_2[1]), .B(B[1]), .VAI_1(add_1_4_vem_1), .S(saida[1]), .VEM_1(add_1_3_vem_1));
  main main_3 ();
  ADD_1 add_1_4 (.A(in_2[0]), .B(B[0]), .VAI_1(VEM_1), .S(saida[0]), .VEM_1(add_1_4_vem_1));
  main main_4 ();

  // Notes on the sheet:
  //   A
endmodule
